# Fritzing sketch breadboard_diagram (saved by Fritzing 0.9.3b)
breadboards: 1

parts:
  Componente1 = Arduino Uno (Rev3)
  C2 = Tantalum Capacitor [capacitance=1μF package="100 mil [THT, tantalum]"]
  C3 = Tantalum Capacitor [capacitance=1μF package="100 mil [THT, tantalum]"]
  C4 = Tantalum Capacitor [capacitance=1μF package="100 mil [THT, tantalum]"]
  C5 = Tantalum Capacitor [capacitance=1μF package="100 mil [THT, tantalum]"]
  C6 = Tantalum Capacitor [capacitance=1μF package="100 mil [THT, tantalum]"]
  C7 = Tantalum Capacitor [capacitance=1μF package="100 mil [THT, tantalum]"]
  S1 = Pushbutton [package="[THT]"]
  R1 = Resistor [tolerance=±5% resistance=220 package=THT]
  R2 = Resistor [tolerance=±5% resistance=220 package=THT]
  R3 = Resistor [tolerance=±5% resistance=220 package=THT]
  R4 = Resistor [tolerance=±5% resistance=220 package=THT]
  R5 = Resistor [tolerance=±5% resistance=220 package=THT]
  R6 = Resistor [tolerance=±5% resistance=220 package=THT]
  R7 = Resistor [tolerance=±5% resistance=220 package=THT]
  Raspberry_Pi_1 = Raspberry Pi 3 [part_number=RPI-3-V1.2]
  R8 = Resistor [tolerance=±5% resistance=220 package=THT]
  R9 = Resistor [tolerance=±5% resistance=220 package=THT]

nets:
  N1: Componente1.D9_PWM, R5.Pin_1
  N2: Componente1.D10_PWM/SS, R6.Pin_1
  N3: Componente1.D11_PWM/MOSI, R7.Pin_1
  N4: Componente1.D2, S1.Pin_3, S1.Pin_4, R1.Pin_1, Raspberry_Pi_1.GIPO25
  N5: Componente1.D3_PWM, R2.Pin_1
  N6: Componente1.D4, Raspberry_Pi_1.GIPO23, R9.Pin_1
  N7: Componente1.D5_PWM, R3.Pin_1
  N8: Componente1.D6_PWM, R4.Pin_1
  N9: Componente1.D7, Raspberry_Pi_1.GIPO24, R8.Pin_1
  N10: Componente1.5V, S1.Pin_1, S1.Pin_2
  N11: Componente1.GND, C2.-, C3.-, C4.-, C5.-, C6.-, C7.-, R1.Pin_0, R8.Pin_0, R9.Pin_0
  N12: C2.+, R7.Pin_0
  N13: C3.+, R6.Pin_0
  N14: C4.+, R5.Pin_0
  N15: C5.+, R4.Pin_0
  N16: C6.+, R3.Pin_0
  N17: C7.+, R2.Pin_0

notes:
  LEDs - Arduino (OUT)
  LED 1 - Pin 11
  LED 2 - Pin 10
  LED 3 - Pin 9
  LED 4 - Pin 6
  LED 5 - Pin 5
  LED 6 - Pin 3
  Conexión Arduino (IN) -> Raspberrypi (OUT)
  Pin 2 -> Boton Efecto -> (GPIO 25)
  Pin 4 -> Boton + Vel -> (GPIO 24)
  Pin 7 -> Boton - Vel -> (GPIO 23)
